// Logisim project Indirect_Adressing_Unit.circ as structural Verilog: 1 circuit, main circuit Indirect_Adressing_Unit
module Indirect_Adressing_Unit (
  input  RESET,
  input  CLK,
  input  [15:0] DATA_0,
  input  [15:0] DATA_1,
  input  [15:0] DATA_2,
  input  INSTRUCTION_READY,
  input  [4:0] INPUT_REG,
  input  [15:0] INPUT_RAM,
  output [15:0] OUTPUT_0,
  output [15:0] OUTPUT_1,
  output [15:0] OUTPUT_2,
  output [4:0] REG_ADRESS,
  output [14:0] RAM_ADRESS
);

  wire adress_comparator_4bit_1_output_adress, adress_comparator_4bit_2_output_adress,
       adress_comparator_4bit_3_output_adress, and_1_out, and_2_out, and_3_out, and_4_out, and_5_out,
       and_6_out, and_7_out, and_8_out, and_9_out, and_10_out, and_11_out, and_12_out, and_13_out,
       and_14_out, and_15_out, and_16_out, and_17_out, and_18_out, and_19_out, and_20_out, and_21_out,
       and_22_out, d_ff_1_q, d_ff_2_q, d_ff_2_qn, d_ff_3_q, d_ff_4_q, d_ff_5_q, d_ff_6_q, d_ff_6_qn,
       d_ff_7_q, d_ff_8_q, d_ff_8_qn, d_ff_9_q, d_ff_10_q, d_ff_10_qn, not_1_out, not_2_out, not_3_out,
       not_4_out, not_5_out, not_6_out, not_7_out, not_8_out, not_9_out, or_3_out, or_4_out, or_5_out,
       or_7_out, or_8_out, or_9_out, or_10_out, or_11_out, subtractor_1_bout;
  wire [2:0] multiplexer_1_out, register_1_q_2, register_2_q_2;
  wire [3:0] multiplexer_2_out, multiplexer_3_out, multiplexer_4_out, register_4_q, register_5_q,
       register_6_q, subtractor_2_out, subtractor_3_out, subtractor_4_out;
  wire [4:0] demultiplexer_1_out1, demultiplexer_2_out1, demultiplexer_3_out0, demultiplexer_4_out1,
       demultiplexer_5_out1, demultiplexer_6_out1, demultiplexer_8_out0, demultiplexer_11_out1;
  wire [14:0] demultiplexer_9_out1, demultiplexer_13_out1;
  wire [15:0] demultiplexer_3_out0_2, demultiplexer_3_out1, demultiplexer_7_out0, demultiplexer_7_out1,
       demultiplexer_8_out0_2, demultiplexer_8_out1, demultiplexer_10_out0, demultiplexer_10_out1,
       demultiplexer_12_out0, or_6_out, register_1_q, register_2_q, register_3_q, register_7_q, register_8_q,
       register_9_q;

  Demultiplexer #(.width(5)) demultiplexer_1 (
    .out1(demultiplexer_1_out1), .in(demultiplexer_3_out0), .sel(and_4_out));  // open: out0
  Demultiplexer #(.width(5)) demultiplexer_2 (
    .out1(demultiplexer_2_out1), .in(demultiplexer_3_out1[14:10]), .sel(and_5_out));  // open: out0
  Demultiplexer #(.width(16)) demultiplexer_3 (
    .out0({demultiplexer_3_out0_2[15:10], demultiplexer_3_out0, demultiplexer_3_out0_2[4:0]}),
    .out1(demultiplexer_3_out1), .in({register_1_q[15:13], register_1_q_2, register_1_q[9:0]}),
    .sel(subtractor_1_bout));
  Demultiplexer #(.width(5)) demultiplexer_4 (
    .out1(demultiplexer_4_out1), .in(demultiplexer_3_out1[9:5]), .sel(and_4_out));  // open: out0
  Demultiplexer #(.width(5)) demultiplexer_5 (
    .out1(demultiplexer_5_out1), .in(demultiplexer_7_out1[4:0]), .sel(and_6_out));  // open: out0
  Subtractor #(.width(5)) subtractor_1 (
    .a(register_1_q[4:0]), .b(5'b10100), .bout(subtractor_1_bout));  // open: out, bin
  Demultiplexer #(.width(5)) demultiplexer_6 (
    .out1(demultiplexer_6_out1), .in(demultiplexer_8_out0), .sel(and_5_out));  // open: out0
  and and_1 (and_1_out, RESET, CLK);
  Demultiplexer #(.width(16)) demultiplexer_7 (
    .out0(demultiplexer_7_out0), .out1(demultiplexer_7_out1),
    .in({register_2_q[15:8], register_2_q_2, register_2_q[4:0]}), .sel(subtractor_1_bout));
  Demultiplexer #(.width(16)) demultiplexer_8 (
    .out0({demultiplexer_8_out0_2[15:6], demultiplexer_8_out0, demultiplexer_8_out0_2[0]}),
    .out1(demultiplexer_8_out1), .in(demultiplexer_7_out0), .sel(demultiplexer_7_out0[0]));
  Demultiplexer #(.width(15)) demultiplexer_9 (
    .out1(demultiplexer_9_out1), .in(demultiplexer_8_out1[15:1]), .sel(and_5_out));  // open: out0
  and and_2 (and_2_out, CLK, d_ff_2_qn);
  Demultiplexer #(.width(16)) demultiplexer_10 (
    .out0(demultiplexer_10_out0), .out1(demultiplexer_10_out1), .in(demultiplexer_12_out0),
    .sel(demultiplexer_12_out0[0]));
  Demultiplexer #(.width(5)) demultiplexer_11 (
    .out1(demultiplexer_11_out1), .in(demultiplexer_10_out0[5:1]), .sel(and_6_out));  // open: out0
  D_Flip_Flop d_ff_1 (.D(1'b1), .clk(and_3_out), .Q(d_ff_1_q), .reset(and_1_out));  // open: Qn, preset
  and and_3 (and_3_out, CLK, INSTRUCTION_READY);
  Register #(.width(16)) register_1 (
    .D(DATA_0), .en(1'b1), .clk(d_ff_1_q), .Q({register_1_q[15:13], register_1_q_2, register_1_q[9:0]}),
    .clr(and_1_out));
  D_Flip_Flop d_ff_2 (
    .D(INSTRUCTION_READY), .clk(and_2_out), .Q(d_ff_2_q), .Qn(d_ff_2_qn), .reset(and_1_out));  // open: preset
  Demultiplexer #(.width(16)) demultiplexer_12 (
    .out0(demultiplexer_12_out0), .in(register_3_q), .sel(subtractor_1_bout));  // open: out1
  Demultiplexer #(.width(15)) demultiplexer_13 (
    .out1(demultiplexer_13_out1), .in(demultiplexer_10_out1[15:1]), .sel(and_6_out));  // open: out0
  D_Flip_Flop d_ff_3 (.D(1'b1), .clk(and_3_out), .Q(d_ff_3_q), .reset(and_1_out));  // open: Qn, preset
  Register #(.width(16)) register_2 (
    .D(DATA_1), .en(1'b1), .clk(d_ff_3_q), .Q({register_2_q[15:8], register_2_q_2, register_2_q[4:0]}),
    .clr(and_1_out));
  not not_1 (not_1_out, and_11_out);
  and and_4 (and_4_out, not_1_out, d_ff_5_q);
  not not_2 (not_2_out, and_16_out);
  and and_5 (and_5_out, not_2_out, d_ff_5_q, and_11_out);
  not not_3 (not_3_out, and_21_out);
  and and_6 (and_6_out, d_ff_5_q, not_3_out, and_11_out, and_16_out);
  D_Flip_Flop d_ff_4 (.D(1'b1), .clk(and_3_out), .Q(d_ff_4_q), .reset(and_1_out));  // open: Qn, preset
  Register #(.width(16)) register_3 (.D(DATA_2), .en(1'b1), .clk(d_ff_4_q), .Q(register_3_q), .clr(and_1_out));
  assign REG_ADRESS = demultiplexer_11_out1 | demultiplexer_6_out1 | demultiplexer_5_out1 | demultiplexer_4_out1 | demultiplexer_2_out1 | demultiplexer_1_out1;  // OR_Gate or_1, 5 bits wide
  D_Flip_Flop d_ff_5 (.D(1'b1), .clk(and_7_out), .Q(d_ff_5_q), .reset(and_1_out));  // open: Qn, preset
  and and_7 (and_7_out, d_ff_2_q, CLK);
  Multiplexer #(.width(3)) multiplexer_1 (
    .in0(register_1_q_2), .in1(register_2_q_2), .out(multiplexer_1_out), .sel(subtractor_1_bout));
  assign RAM_ADRESS = demultiplexer_13_out1 | demultiplexer_9_out1;  // OR_Gate or_2, 15 bits wide
  not not_4 (not_4_out, multiplexer_1_out[0]);
  not not_5 (not_5_out, multiplexer_1_out[1]);
  not not_6 (not_6_out, multiplexer_1_out[2]);
  D_Flip_Flop d_ff_6 (
    .D(multiplexer_1_out[0]), .clk(CLK), .Q(d_ff_6_q), .Qn(d_ff_6_qn), .reset(and_1_out));  // open: preset
  and and_8 (and_8_out, d_ff_5_q, d_ff_6_qn);
  and and_9 (and_9_out, not_7_out, d_ff_5_q);
  or or_3 (or_3_out, and_9_out, and_8_out);
  not not_7 (not_7_out, adress_comparator_4bit_1_output_adress);
  Register #(.width(4)) register_4 (
    .D(multiplexer_2_out), .en(1'b1), .clk(and_10_out), .Q(register_4_q), .clr(and_1_out));
  Multiplexer #(.width(4)) multiplexer_2 (
    .in0(subtractor_2_out), .in1(4'b0100), .out(multiplexer_2_out), .sel(d_ff_6_qn));
  and and_10 (and_10_out, or_3_out, multiplexer_1_out[0], CLK);
  and and_11 (and_11_out, d_ff_5_q, or_4_out);
  Subtractor #(.width(4)) subtractor_2 (.a(register_4_q), .b(4'b0001), .out(subtractor_2_out));  // open: bin, bout
  and and_12 (and_12_out, d_ff_5_q, not_4_out);
  and and_13 (and_13_out, d_ff_6_q, adress_comparator_4bit_1_output_adress);
  or or_4 (or_4_out, not_4_out, or_5_out);
  D_Flip_Flop d_ff_7 (.D(or_5_out), .clk(CLK), .Q(d_ff_7_q), .reset(and_1_out));  // open: Qn, preset
  or or_5 (or_5_out, and_12_out, and_13_out);
  Adress_Comparator_4bit adress_comparator_4bit_1 (
    .ADRESS(register_4_q), .PHYSICAL_ADRESS(4'b0000), .OUTPUT_ADRESS(adress_comparator_4bit_1_output_adress));
  assign or_6_out = {{11{1'b0}}, INPUT_REG} | INPUT_RAM;  // OR_Gate or_6, 16 bits wide
  D_Flip_Flop d_ff_8 (
    .D(multiplexer_1_out[1]), .clk(CLK), .Q(d_ff_8_q), .Qn(d_ff_8_qn), .reset(and_1_out));  // open: preset
  and and_14 (and_14_out, not_8_out, d_ff_7_q);
  or or_7 (or_7_out, and_14_out, d_ff_8_qn);
  not not_8 (not_8_out, adress_comparator_4bit_2_output_adress);
  Register #(.width(4)) register_5 (
    .D(multiplexer_3_out), .en(1'b1), .clk(and_15_out), .Q(register_5_q), .clr(and_1_out));
  Multiplexer #(.width(4)) multiplexer_3 (
    .in0(subtractor_3_out), .in1(4'b0100), .out(multiplexer_3_out), .sel(d_ff_8_qn));
  and and_15 (and_15_out, or_7_out, multiplexer_1_out[1], CLK);
  Subtractor #(.width(4)) subtractor_3 (.a(register_5_q), .b(4'b0001), .out(subtractor_3_out));  // open: bin, bout
  and and_16 (and_16_out, d_ff_5_q, or_8_out);
  or or_8 (or_8_out, not_5_out, or_9_out);
  and and_17 (and_17_out, d_ff_7_q, not_5_out);
  and and_18 (and_18_out, d_ff_8_q, adress_comparator_4bit_2_output_adress);
  or or_9 (or_9_out, and_17_out, and_18_out);
  Adress_Comparator_4bit adress_comparator_4bit_2 (
    .ADRESS(register_5_q), .PHYSICAL_ADRESS(4'b0000), .OUTPUT_ADRESS(adress_comparator_4bit_2_output_adress));
  D_Flip_Flop d_ff_9 (.D(or_9_out), .clk(CLK), .Q(d_ff_9_q), .reset(and_1_out));  // open: Qn, preset
  D_Flip_Flop d_ff_10 (
    .D(multiplexer_1_out[2]), .clk(CLK), .Q(d_ff_10_q), .Qn(d_ff_10_qn), .reset(and_1_out));  // open: preset
  not not_9 (not_9_out, adress_comparator_4bit_3_output_adress);
  and and_19 (and_19_out, not_9_out, d_ff_9_q);
  or or_10 (or_10_out, and_19_out, d_ff_10_qn);
  Subtractor #(.width(4)) subtractor_4 (.a(register_6_q), .b(4'b0001), .out(subtractor_4_out));  // open: bin, bout
  Register #(.width(4)) register_6 (
    .D(multiplexer_4_out), .en(1'b1), .clk(and_20_out), .Q(register_6_q), .clr(and_1_out));
  Multiplexer #(.width(4)) multiplexer_4 (
    .in0(subtractor_4_out), .in1(4'b0100), .out(multiplexer_4_out), .sel(d_ff_10_qn));
  and and_20 (and_20_out, or_10_out, multiplexer_1_out[2], CLK);
  and and_21 (and_21_out, d_ff_5_q, or_11_out);
  or or_11 (or_11_out, not_6_out, and_22_out);
  and and_22 (and_22_out, d_ff_10_q, adress_comparator_4bit_3_output_adress);
  Adress_Comparator_4bit adress_comparator_4bit_3 (
    .ADRESS(register_6_q), .PHYSICAL_ADRESS(4'b0000), .OUTPUT_ADRESS(adress_comparator_4bit_3_output_adress));
  Register #(.width(16)) register_7 (.D(or_6_out), .en(1'b1), .clk(and_11_out), .Q(register_7_q));  // open: clr
  Register #(.width(16)) register_8 (.D(or_6_out), .en(1'b1), .clk(and_16_out), .Q(register_8_q));  // open: clr
  Register #(.width(16)) register_9 (.D(or_6_out), .en(1'b1), .clk(and_21_out), .Q(register_9_q));  // open: clr
endmodule
